// Logisim project DCnetExample.circ as structural Verilog: 1 circuit, main circuit main
module main (
);

  wire A_Message_out, A_out, A_Public_Message, and_1_out, B_Message_out, B_out, B_Public_Message,
       C_Message_out, C_out, C_Public_Message, Clear_2_out, Clear_3_out, Clear_4_out, Clear_out, clock_1_out,
       clock_2_out, clock_3_out, clock_4_out, clock_5_out, clock_6_out, clock_7_out, clock_8_out, or_1_out,
       Secret_A_B, Secret_B_C, Secret_C_A, xor_1_out, xor_2_out;
  wire [6:0] keyboard_1_data, keyboard_2_data, keyboard_3_data, or_2_out;
  wire [7:0] A_2_out, A_Public_M, and_2_out, B_2_out, B_Public_M, C_2_out, C_Public_M, Secret_A_B_t,
       Secret_B_C_t, Secret_C_A_t, xor_3_out, xor_4_out;
  wire [7:1] random_1_out;
  wire [7:7] keyboard_1_avail, keyboard_2_avail, keyboard_3_avail, or_2_out_2;

  Random random_1 (
    .clk(clock_1_out), .next(clock_1_out),
    .out({random_1_out[7], Secret_C_A, random_1_out[5:4], Secret_B_C, random_1_out[2:1], Secret_A_B}));  // open: clr
  Clock #(.highDuration(2), .lowDuration(2)) clock_1 (.out(clock_1_out));
  Clock #(.highDuration(2), .lowDuration(2)) clock_2 (.out(clock_2_out));
  Clock #(.lowDuration(2)) clock_3 (.out(clock_3_out));
  Clock #(.highDuration(5)) clock_4 (.out(clock_4_out));
  Random random_2 (.clk(clock_2_out), .next(clock_2_out), .out(Secret_A_B_t));  // open: clr
  Random random_3 (.clk(clock_3_out), .next(clock_3_out), .out(Secret_B_C_t));  // open: clr
  Random #(.seed(10)) random_4 (.clk(clock_4_out), .next(clock_4_out), .out(Secret_C_A_t));  // open: clr
  LED led_1 (.in(Secret_A_B));
  LED led_2 (.in(random_1_out[1]));
  LED led_3 (.in(random_1_out[2]));
  LED led_4 (.in(Secret_B_C));
  LED led_5 (.in(random_1_out[4]));
  LED led_6 (.in(random_1_out[5]));
  LED led_7 (.in(Secret_C_A));
  LED led_8 (.in(random_1_out[7]));
  // Probe on Secret_A_B_t
  // Probe on Secret_B_C_t
  // Probe on Secret_C_A_t
  Clock clock_5 (.out(clock_5_out));
  Clock clock_6 (.out(clock_6_out));
  Clock clock_7 (.out(clock_7_out));
  Button A_Message (.out(A_Message_out));
  xor A (A_out, Secret_A_B, Secret_C_A);
  Button B_Message (.out(B_Message_out));
  xor B (B_out, Secret_A_B, Secret_B_C);
  Button C_Message (.out(C_Message_out));
  xor C (C_out, Secret_C_A, Secret_B_C);
  Keyboard keyboard_1 (
    .clk(clock_5_out), .re(1'b1), .clr(Clear_out), .avail(keyboard_1_avail[7]), .data(keyboard_1_data));
  Button Clear (.out(Clear_out));
  assign A_2_out = Secret_A_B_t ^ Secret_C_A_t;  // XOR_Gate A_2, 8 bits wide
  Keyboard keyboard_2 (
    .clk(clock_6_out), .re(1'b1), .clr(Clear_2_out), .avail(keyboard_2_avail[7]), .data(keyboard_2_data));
  Button Clear_2 (.out(Clear_2_out));
  assign B_2_out = Secret_A_B_t ^ Secret_B_C_t;  // XOR_Gate B_2, 8 bits wide
  Keyboard keyboard_3 (
    .clk(clock_7_out), .re(1'b1), .clr(Clear_3_out), .avail(keyboard_3_avail[7]), .data(keyboard_3_data));
  Button Clear_3 (.out(Clear_3_out));
  assign C_2_out = Secret_C_A_t ^ Secret_B_C_t;  // XOR_Gate C_2, 8 bits wide
  xor A_3 (A_Public_Message, A_Message_out, A_out);
  xor B_3 (B_Public_Message, B_Message_out, B_out);
  xor C_3 (C_Public_Message, C_Message_out, C_out);
  LED led_9 (.in(A_Public_Message));
  LED led_10 (.in(B_Public_Message));
  LED led_11 (.in(C_Public_Message));
  assign A_Public_M = {keyboard_1_avail[7], keyboard_1_data} ^ A_2_out;  // XOR_Gate A_4, 8 bits wide
  assign B_Public_M = {keyboard_2_avail[7], keyboard_2_data} ^ B_2_out;  // XOR_Gate A_5, 8 bits wide
  assign C_Public_M = {keyboard_3_avail[7], keyboard_3_data} ^ C_2_out;  // XOR_Gate A_6, 8 bits wide
  LED led_12 (.in(A_Public_M[0]));
  LED led_13 (.in(A_Public_M[1]));
  LED led_14 (.in(A_Public_M[2]));
  LED led_15 (.in(A_Public_M[3]));
  LED led_16 (.in(A_Public_M[4]));
  LED led_17 (.in(A_Public_M[5]));
  LED led_18 (.in(A_Public_M[6]));
  LED led_19 (.in(A_Public_M[7]));
  LED led_20 (.in(B_Public_M[0]));
  LED led_21 (.in(B_Public_M[1]));
  LED led_22 (.in(B_Public_M[2]));
  LED led_23 (.in(B_Public_M[3]));
  LED led_24 (.in(B_Public_M[4]));
  LED led_25 (.in(B_Public_M[5]));
  LED led_26 (.in(B_Public_M[6]));
  LED led_27 (.in(B_Public_M[7]));
  LED led_28 (.in(C_Public_M[0]));
  LED led_29 (.in(C_Public_M[1]));
  LED led_30 (.in(C_Public_M[2]));
  LED led_31 (.in(C_Public_M[3]));
  LED led_32 (.in(C_Public_M[4]));
  LED led_33 (.in(C_Public_M[5]));
  LED led_34 (.in(C_Public_M[6]));
  LED led_35 (.in(C_Public_M[7]));
  and and_1 (and_1_out, A_Public_Message, B_Public_Message, C_Public_Message);
  xor xor_1 (xor_1_out, A_Public_Message, B_Public_Message);
  LED led_36 (.in(or_2_out[0]));
  LED led_37 (.in(or_2_out[1]));
  LED led_38 (.in(or_2_out[2]));
  LED led_39 (.in(or_2_out[3]));
  LED led_40 (.in(or_2_out[4]));
  LED led_41 (.in(or_2_out[5]));
  LED led_42 (.in(or_2_out[6]));
  LED led_43 (.in(or_2_out_2[7]));
  or or_1 (or_1_out, and_1_out, xor_2_out);
  xor xor_2 (xor_2_out, xor_1_out, C_Public_Message);
  // Probe on or_1_out
  assign xor_3_out = A_Public_M ^ B_Public_M;  // XOR_Gate xor_3, 8 bits wide
  TTY tty_1 (.data(or_2_out), .clk(clock_8_out), .we(or_2_out_2[7]), .clr(Clear_4_out));
  Clock clock_8 (.out(clock_8_out));
  Button Clear_4 (.out(Clear_4_out));
  assign and_2_out = A_Public_M & B_Public_M & C_Public_M;  // AND_Gate and_2, 8 bits wide
  assign xor_4_out = xor_3_out ^ C_Public_M;  // XOR_Gate xor_4, 8 bits wide
  assign {or_2_out_2[7], or_2_out} = and_2_out | xor_4_out;  // OR_Gate or_2, 8 bits wide
  // Probe on {or_2_out_2[7], or_2_out}

  // Notes on the sheet:
  //   Phase 1 - Shared Secrets
  //   Phase 1 - Shared Secrets
  //   Phase 2 - Broadcast Message
  //   Phase 2 - Broadcast Message
  //   Phase 3 - Interpret Group  Message
  //   Phase 3 - Interpret Group  Message
endmodule
