// Logisim project DCnetLogisim.circ as structural Verilog: 1 circuit, main circuit main
module main (
);

  wire A_2_out, A_Message_out, A_Public_Message, and_1_out, B_2_out, B_Message_out, B_Public_Message,
       C_2_out, C_Message_out, C_Public_Message, Clear_2_out, Clear_3_out, Clear_4_out, Clear_out,
       clock_4_out, clock_5_out, clock_6_out, clock_7_out, clock_8_out, clock_9_out, clock_10_out, or_1_out,
       Secret_A_B, Secret_B_C, Secret_C_A, xor_1_out, xor_3_out;
  wire [6:0] keyboard_1_data, keyboard_2_data, keyboard_3_data, or_2_out;
  wire [7:0] A_out, A_Public_M, and_2_out, B_out, B_Public_M, C_out, C_Public_M, Secret_A_B_t, Secret_B_C_t,
       Secret_C_A_t, xor_2_out, xor_4_out;
  wire [7:7] keyboard_1_avail, keyboard_2_avail, keyboard_3_avail, or_2_out_2;

  Clock #(.lowDuration(3)) clock_1 (.out(Secret_A_B));
  Clock #(.highDuration(2), .lowDuration(3)) clock_2 (.out(Secret_B_C));
  Clock #(.highDuration(4), .lowDuration(3)) clock_3 (.out(Secret_C_A));
  Clock #(.highDuration(2), .lowDuration(2)) clock_4 (.out(clock_4_out));
  Clock #(.lowDuration(2)) clock_5 (.out(clock_5_out));
  Clock #(.highDuration(2)) clock_6 (.out(clock_6_out));
  Random random_1 (.clk(clock_4_out), .next(clock_4_out), .out(Secret_A_B_t));  // open: clr
  Random random_2 (.clk(clock_5_out), .next(clock_5_out), .out(Secret_B_C_t));  // open: clr
  Random random_3 (.clk(clock_6_out), .next(clock_6_out), .out(Secret_C_A_t));  // open: clr
  Clock clock_7 (.out(clock_7_out));
  Keyboard keyboard_1 (
    .clk(clock_7_out), .re(1'b1), .clr(Clear_out), .avail(keyboard_1_avail[7]), .data(keyboard_1_data));
  Clock clock_8 (.out(clock_8_out));
  Keyboard keyboard_2 (
    .clk(clock_8_out), .re(1'b1), .clr(Clear_2_out), .avail(keyboard_2_avail[7]), .data(keyboard_2_data));
  Keyboard keyboard_3 (
    .clk(clock_9_out), .re(1'b1), .clr(Clear_3_out), .avail(keyboard_3_avail[7]), .data(keyboard_3_data));
  Clock clock_9 (.out(clock_9_out));
  // Probe on Secret_A_B_t
  // Probe on Secret_B_C_t
  // Probe on Secret_C_A_t
  Button Clear (.out(Clear_out));
  assign A_out = Secret_A_B_t ^ Secret_C_A_t;  // XOR_Gate A, 8 bits wide
  Button Clear_2 (.out(Clear_2_out));
  assign B_out = Secret_A_B_t ^ Secret_B_C_t;  // XOR_Gate B, 8 bits wide
  Button Clear_3 (.out(Clear_3_out));
  assign C_out = Secret_C_A_t ^ Secret_B_C_t;  // XOR_Gate C, 8 bits wide
  xor A_2 (A_2_out, Secret_A_B, Secret_C_A);
  xor B_2 (B_2_out, Secret_A_B, Secret_B_C);
  xor C_2 (C_2_out, Secret_C_A, Secret_B_C);
  Button A_Message (.out(A_Message_out));
  Button B_Message (.out(B_Message_out));
  Button C_Message (.out(C_Message_out));
  assign A_Public_M = {keyboard_1_avail[7], keyboard_1_data} ^ A_out;  // XOR_Gate A_3, 8 bits wide
  assign B_Public_M = {keyboard_2_avail[7], keyboard_2_data} ^ B_out;  // XOR_Gate A_4, 8 bits wide
  assign C_Public_M = {keyboard_3_avail[7], keyboard_3_data} ^ C_out;  // XOR_Gate A_5, 8 bits wide
  xor A_6 (A_Public_Message, A_Message_out, A_2_out);
  LED led_1 (.in(A_Public_Message));
  LED led_2 (.in(B_Public_Message));
  xor B_3 (B_Public_Message, B_Message_out, B_2_out);
  LED led_3 (.in(C_Public_Message));
  xor C_3 (C_Public_Message, C_Message_out, C_2_out);
  LED led_4 (.in(A_Public_M[0]));
  LED led_5 (.in(A_Public_M[1]));
  LED led_6 (.in(A_Public_M[2]));
  LED led_7 (.in(A_Public_M[3]));
  LED led_8 (.in(A_Public_M[4]));
  LED led_9 (.in(A_Public_M[5]));
  LED led_10 (.in(A_Public_M[6]));
  LED led_11 (.in(A_Public_M[7]));
  LED led_12 (.in(B_Public_M[0]));
  LED led_13 (.in(B_Public_M[1]));
  LED led_14 (.in(B_Public_M[2]));
  LED led_15 (.in(B_Public_M[3]));
  LED led_16 (.in(B_Public_M[4]));
  LED led_17 (.in(B_Public_M[5]));
  LED led_18 (.in(B_Public_M[6]));
  LED led_19 (.in(B_Public_M[7]));
  LED led_20 (.in(C_Public_M[0]));
  LED led_21 (.in(C_Public_M[1]));
  LED led_22 (.in(C_Public_M[2]));
  LED led_23 (.in(C_Public_M[3]));
  LED led_24 (.in(C_Public_M[4]));
  LED led_25 (.in(C_Public_M[5]));
  LED led_26 (.in(C_Public_M[6]));
  LED led_27 (.in(C_Public_M[7]));
  and and_1 (and_1_out, A_Public_Message, B_Public_Message, C_Public_Message);
  xor xor_1 (xor_1_out, A_Public_Message, B_Public_Message);
  assign and_2_out = A_Public_M & B_Public_M & C_Public_M;  // AND_Gate and_2, 8 bits wide
  assign xor_2_out = A_Public_M ^ B_Public_M;  // XOR_Gate xor_2, 8 bits wide
  or or_1 (or_1_out, and_1_out, xor_3_out);
  xor xor_3 (xor_3_out, xor_1_out, C_Public_Message);
  assign {or_2_out_2[7], or_2_out} = and_2_out | xor_4_out;  // OR_Gate or_2, 8 bits wide
  assign xor_4_out = xor_2_out ^ C_Public_M;  // XOR_Gate xor_4, 8 bits wide
  LED led_28 (.in(or_2_out[0]));
  LED led_29 (.in(or_2_out[1]));
  LED led_30 (.in(or_2_out[2]));
  LED led_31 (.in(or_2_out[3]));
  LED led_32 (.in(or_2_out[4]));
  LED led_33 (.in(or_2_out[5]));
  LED led_34 (.in(or_2_out[6]));
  LED led_35 (.in(or_2_out_2[7]));
  // Probe on or_1_out
  // Probe on {or_2_out_2[7], or_2_out}
  TTY tty_1 (.data(or_2_out), .clk(clock_10_out), .we(or_2_out_2[7]), .clr(Clear_4_out));
  Button Clear_4 (.out(Clear_4_out));
  Clock clock_10 (.out(clock_10_out));
endmodule
