// Logisim project DCnetscaled.circ as structural Verilog: 1 circuit, main circuit main
module main (
);

  wire Clear_2_out, Clear_3_out, Clear_4_out, Clear_5_out, Clear_6_out, Clear_out, clock_1_out, clock_2_out,
       clock_3_out, clock_4_out, clock_5_out, clock_6_out, clock_7_out, clock_8_out, clock_9_out,
       clock_10_out, clock_11_out;
  wire [6:0] keyboard_1_data, keyboard_2_data, keyboard_3_data, keyboard_4_data, keyboard_5_data;
  wire [7:0] A_out, A_Public_M, B_out, B_Public_M, C_out, C_Public_M, D_out, D_Public_M, E_out, E_Public_M,
       Secret_A_B, Secret_B_C, Secret_C_D, Secret_D_E, Secret_E_A, xor_1_out, xor_2_out, xor_3_out, xor_4_out;
  wire [7:7] keyboard_1_avail, keyboard_2_avail, keyboard_3_avail, keyboard_4_avail, keyboard_5_avail;

  Keyboard keyboard_1 (
    .clk(clock_1_out), .re(1'b1), .clr(Clear_out), .avail(keyboard_1_avail[7]), .data(keyboard_1_data));
  Clock clock_1 (.out(clock_1_out));
  Button Clear (.out(Clear_out));
  assign A_out = Secret_A_B ^ Secret_E_A;  // XOR_Gate A, 8 bits wide
  Clock clock_2 (.out(clock_2_out));
  Keyboard keyboard_2 (
    .clk(clock_2_out), .re(1'b1), .clr(Clear_2_out), .avail(keyboard_2_avail[7]), .data(keyboard_2_data));
  Button Clear_2 (.out(Clear_2_out));
  assign B_out = Secret_A_B ^ Secret_B_C;  // XOR_Gate B, 8 bits wide
  Keyboard keyboard_3 (
    .clk(clock_3_out), .re(1'b1), .clr(Clear_3_out), .avail(keyboard_3_avail[7]), .data(keyboard_3_data));
  Clock clock_3 (.out(clock_3_out));
  Button Clear_3 (.out(Clear_3_out));
  assign C_out = Secret_B_C ^ Secret_C_D;  // XOR_Gate C, 8 bits wide
  Keyboard keyboard_4 (
    .clk(clock_4_out), .re(1'b1), .clr(Clear_4_out), .avail(keyboard_4_avail[7]), .data(keyboard_4_data));
  Clock clock_4 (.out(clock_4_out));
  Button Clear_4 (.out(Clear_4_out));
  assign D_out = Secret_C_D ^ Secret_D_E;  // XOR_Gate D, 8 bits wide
  Clock clock_5 (.out(clock_5_out));
  Keyboard keyboard_5 (
    .clk(clock_5_out), .re(1'b1), .clr(Clear_5_out), .avail(keyboard_5_avail[7]), .data(keyboard_5_data));
  Button Clear_5 (.out(Clear_5_out));
  assign E_out = Secret_D_E ^ Secret_E_A;  // XOR_Gate E, 8 bits wide
  assign A_Public_M = {keyboard_1_avail[7], keyboard_1_data} ^ A_out;  // XOR_Gate A_2, 8 bits wide
  assign B_Public_M = {keyboard_2_avail[7], keyboard_2_data} ^ B_out;  // XOR_Gate B_2, 8 bits wide
  assign C_Public_M = {keyboard_3_avail[7], keyboard_3_data} ^ C_out;  // XOR_Gate C_2, 8 bits wide
  assign D_Public_M = {keyboard_4_avail[7], keyboard_4_data} ^ D_out;  // XOR_Gate D_2, 8 bits wide
  assign E_Public_M = {keyboard_5_avail[7], keyboard_5_data} ^ E_out;  // XOR_Gate E_2, 8 bits wide
  LED led_1 (.in(A_Public_M[0]));
  LED led_2 (.in(A_Public_M[2]));
  LED led_3 (.in(A_Public_M[4]));
  LED led_4 (.in(A_Public_M[6]));
  LED led_5 (.in(B_Public_M[0]));
  LED led_6 (.in(B_Public_M[2]));
  LED led_7 (.in(B_Public_M[4]));
  LED led_8 (.in(B_Public_M[6]));
  LED led_9 (.in(C_Public_M[0]));
  LED led_10 (.in(C_Public_M[2]));
  LED led_11 (.in(C_Public_M[4]));
  LED led_12 (.in(C_Public_M[6]));
  LED led_13 (.in(D_Public_M[0]));
  LED led_14 (.in(D_Public_M[2]));
  LED led_15 (.in(D_Public_M[4]));
  LED led_16 (.in(D_Public_M[6]));
  LED led_17 (.in(E_Public_M[0]));
  LED led_18 (.in(E_Public_M[2]));
  LED led_19 (.in(E_Public_M[4]));
  LED led_20 (.in(E_Public_M[6]));
  LED led_21 (.in(A_Public_M[1]));
  LED led_22 (.in(A_Public_M[3]));
  LED led_23 (.in(A_Public_M[5]));
  LED led_24 (.in(A_Public_M[7]));
  LED led_25 (.in(B_Public_M[1]));
  LED led_26 (.in(B_Public_M[3]));
  LED led_27 (.in(B_Public_M[5]));
  LED led_28 (.in(B_Public_M[7]));
  LED led_29 (.in(C_Public_M[1]));
  LED led_30 (.in(C_Public_M[3]));
  LED led_31 (.in(C_Public_M[5]));
  LED led_32 (.in(C_Public_M[7]));
  LED led_33 (.in(D_Public_M[1]));
  LED led_34 (.in(D_Public_M[3]));
  LED led_35 (.in(D_Public_M[5]));
  LED led_36 (.in(D_Public_M[7]));
  LED led_37 (.in(E_Public_M[1]));
  LED led_38 (.in(E_Public_M[3]));
  LED led_39 (.in(E_Public_M[5]));
  LED led_40 (.in(E_Public_M[7]));
  Clock clock_6 (.out(clock_6_out));
  Clock clock_7 (.out(clock_7_out));
  Clock clock_8 (.out(clock_8_out));
  Clock clock_9 (.out(clock_9_out));
  Clock clock_10 (.out(clock_10_out));
  assign xor_1_out = A_Public_M ^ B_Public_M;  // XOR_Gate xor_1, 8 bits wide
  assign xor_2_out = xor_1_out ^ C_Public_M;  // XOR_Gate xor_2, 8 bits wide
  Random random_1 (.clk(clock_6_out), .next(clock_6_out), .out(Secret_A_B));  // open: clr
  Random #(.seed(1)) random_2 (.clk(clock_7_out), .next(clock_7_out), .out(Secret_B_C));  // open: clr
  Random #(.seed(2)) random_3 (.clk(clock_8_out), .next(clock_8_out), .out(Secret_C_D));  // open: clr
  Random #(.seed(3)) random_4 (.clk(clock_9_out), .next(clock_9_out), .out(Secret_D_E));  // open: clr
  Random #(.seed(4)) random_5 (.clk(clock_10_out), .next(clock_10_out), .out(Secret_E_A));  // open: clr
  assign xor_3_out = xor_2_out ^ D_Public_M;  // XOR_Gate xor_3, 8 bits wide
  LED led_41 (.in(xor_4_out[6]));
  LED led_42 (.in(xor_4_out[4]));
  LED led_43 (.in(xor_4_out[2]));
  LED led_44 (.in(xor_4_out[5]));
  LED led_45 (.in(xor_4_out[7]));
  LED led_46 (.in(xor_4_out[1]));
  LED led_47 (.in(xor_4_out[3]));
  // Probe on Secret_A_B
  // Probe on Secret_B_C
  // Probe on Secret_C_D
  // Probe on Secret_D_E
  // Probe on Secret_E_A
  assign xor_4_out = xor_3_out ^ E_Public_M;  // XOR_Gate xor_4, 8 bits wide
  LED led_48 (.in(xor_4_out[0]));
  // Probe on xor_4_out
  TTY tty_1 (.data(xor_4_out[6:0]), .clk(clock_11_out), .we(xor_4_out[7]), .clr(Clear_6_out));
  Clock clock_11 (.out(clock_11_out));
  Button Clear_6 (.out(Clear_6_out));
endmodule
